// Digital circuit BasicReg1.dig as structural Verilog
module BasicReg1 (
  input  E,
  input  CLK,
  input  R,
  input  D,
  input  S,
  output Q
);

  wire and_1_out;

  and and_1 (and_1_out, E, CLK);
  D_FF_AS d_ff_as_1 (.Set(S), .D(D), .C(and_1_out), .Clr(R), .Q(Q));  // open: nQ
endmodule
