// Digital circuit BasicReg8.dig as structural Verilog
module BasicReg8 (
  input  E,
  input  CLK,
  input  [7:0] D,
  output [7:0] Q
);

  wire and_1_out;

  and and_1 (and_1_out, E, CLK);
  D_FF #(.Bits(8)) d_ff_1 (.D(D), .C(and_1_out), .Q(Q));  // open: nQ
endmodule
