// Digital circuit CPU8Bit1K.dig as structural Verilog
module CPU8Bit1K (
  input  RST,
  input  [7:0] IN,
  input  Clock,
  input  [7:0] PromIN,
  output [7:0] OUT,
  output [9:0] AddrBus,
  output OutE,
  output InE,
  output [9:0] PromAddr
);

  wire AE, AINC, AluBMux, AMux, and_1_out, ARE, ARINC, BE, BINC, BusMux0, BusMux1, C, CCLR, CE, Cout, CSET,
       E, G, IRZ, multiplexer_2_out, N, OP0, OP1, OP2, OP3, PCM0, PCM1, PCM2, PRomAMux, RamAMux, RamE, RamOE,
       Reserva, S, Z;
  wire [1:0] A89;
  wire [5:0] IR;
  wire [7:0] A, alu8bits_1_y, B, multiplexer_1_out, multiplexer_4_out, ramdualport_1_d;
  wire [7:6] alu8bits_1_st;
  wire [9:0] AR, PC;

  Multiplexer #(.Bits(8)) multiplexer_1 (.sel(AMux), .in_0(alu8bits_1_y), .in_1(B), .out(multiplexer_1_out));
  Multiplexer #(.Selector_Bits(3)) multiplexer_2 (
    .sel({PCM2, PCM1, PCM0}), .in_0(1'b0), .in_1(1'b1), .in_2(Z), .in_3(E), .in_4(G), .in_5(S), .in_6(N),
    .in_7(C), .out(multiplexer_2_out));
  // Probe PC on PC
  // Probe BUS on OUT
  // Probe A on A
  // Probe B on B
  // Probe AR on AR
  // Probe IR on {A89, IR}
  // Probe Cout on Cout
  // Probe C on C
  Reg8i A_2 (.E(AE), .INC(AINC), .CLK(Clock), .R(RST), .D(multiplexer_1_out), .Q(A));
  Reg10ir PC_2 (.E(multiplexer_2_out), .INC(1'b1), .nCLK(Clock), .R(RST), .D({A89, PromIN}), .Q(PC));
  and and_1 (and_1_out, PRomAMux, ~Clock);  // And
  ALU8Bits alu8bits_1 (
    .Y(alu8bits_1_y), .A(A), .B(multiplexer_4_out), .ST({alu8bits_1_st, Cout, N, S, G, E, Z}), .Cin(C),
    .OP({OP3, OP2, OP1, OP0}));
  Multiplexer #(.Bits(10)) multiplexer_3 (.sel(and_1_out), .in_0(PC), .in_1(AR), .out(PromAddr));
  Reg8i B_2 (.E(BE), .INC(BINC), .CLK(Clock), .R(RST), .D(OUT), .Q(B));
  Multiplexer #(.Bits(8)) multiplexer_4 (.sel(AluBMux), .in_0(OUT), .in_1(B), .out(multiplexer_4_out));
  // Probe BusMux0 on BusMux0
  // Probe BusMux1 on BusMux1
  // Probe AluBMux on AluBMux
  // Probe IRZ on IRZ
  // Probe PRomAMux on PRomAMux
  // Probe RamAMux on RamAMux
  // Probe RamOU on RamOE
  // Probe RamE on RamE
  Reg10i AR_2 (.E(ARE), .INC(ARINC), .CLK(Clock), .R(RST), .D({A89, OUT}), .Q(AR));
  Multiplexer #(.Bits(10)) multiplexer_5 (.sel(RamAMux), .in_0(AR), .in_1({A89, PromIN}), .out(AddrBus));
  BasicReg1 C_CARRY (.Q(C), .S(CSET), .D(Cout), .E(CE), .CLK(Clock), .CLR(CCLR), .R(RST));
  RAMDualPort #(.AddrBits(4), .Bits(8)) ramdualport_1 (
    .A(AddrBus[3:0]), .Din(OUT), .str(RamE), .C(Clock), .ld(RamOE), .D(ramdualport_1_d));
  // Probe INE on InE
  Multiplexer #(.Selector_Bits(2), .Bits(8)) multiplexer_6 (
    .sel({BusMux1, BusMux0}), .in_0(alu8bits_1_y), .in_1(IN), .in_2(PromIN), .in_3(ramdualport_1_d), .out(OUT));
  // Probe OP0 on OP0
  // Probe OP1 on OP1
  // Probe OP2 on OP2
  // Probe OP3 on OP3
  // Probe PCM0 on PCM0
  // Probe PCM1 on PCM1
  // Probe PCM2 on PCM2
  Reg8 IR_2 (.D(PromIN), .Q({A89, IR}), .SR(IRZ), .nCLK(Clock));
  // Probe OUTE on OutE
  // Probe AE on AE
  // Probe AINC on AINC
  // Probe BE on BE
  // Probe BINC on BINC
  // Probe ARE on ARE
  // Probe ARINC on ARINC
  // Probe CSET on CSET
  ROM #(.AddrBits(6), .Bits(28)) Ctrl (
    .A(IR), .sel(1'b1),
    .D({Reserva, AMux, CCLR, CE, CSET, ARINC, ARE, BINC, BE, AINC, AE, OutE, InE, PCM2, PCM1, PCM0, OP3, OP2, OP1, OP0, RamE, RamOE, RamAMux, PRomAMux, IRZ, AluBMux, BusMux1, BusMux0}));
  // Probe CE on CE
  // Probe CCLR on CCLR
  // Probe AMux on AMux
  // Probe Reserva on Reserva

  // Other names for the same wires on the sheet: BUS[7:0] = OUT; CLK = Clock; IR[7:6] = A89; PROM[7:0] = PromIN;
  //   RESET = RST

  // Notes on the sheet:
  //   RST: default 1
  //   Clock: Hz: 10
  //   Version 0.3
  //   contents of Ctrl (hex, n*v repeats v):
  //   0,2010a,8000a,20000a,20112,80012,420112,480012,80000,20104,80
  //   ,184,400080,400184,a8,1ac,20143,80043,420143,480043,2016b,8006b
  //   ,28101,88001,428101,488001,28129,88029,10000,10104,1000a,410000
  //   ,410104,41000a,10028,1012c,40000,100000,400000,1008,2008,300c
  //   ,400c,500c,6008,7008,1800000,3000000,20200,20304,2030a,20404,2040a
  //   ,20504,2050a,1020604,102060a,1020704,102070a,1020800,1080904,1020a00
  //   ,1020b00,40a0000
endmodule
