// Digital circuit Reg8.dig as structural Verilog
module Reg8 (
  input  [7:0] D,
  input  nCLK,
  input  SR,
  output [7:0] Q
);

  wire [7:0] multiplexer_1_out;

  Multiplexer #(.Bits(8)) multiplexer_1 (.sel(SR), .in_0(D), .in_1({8{1'b0}}), .out(multiplexer_1_out));
  D_FF #(.Bits(8)) d_ff_1 (.D(multiplexer_1_out), .C(~nCLK), .Q(Q));  // open: nQ
endmodule
