// Digital circuit TesteCpuDidatica.dig as structural Verilog
module TesteCpuDidatica (
  input  Clock,
  input  Reset,
  output a,
  output b,
  output c,
  output d,
  output e,
  output f,
  output g,
  output dig0,
  output dig1,
  output L0,
  output L1,
  output L2,
  output L3
);

  wire and_1_out, and_2_out, cpu8bit1k_1_oute, div50m10hz_1_y, not_1_out;
  wire [3:0] multiplexer_1_out;
  wire [7:0] cpu8bit1k_1_out, PROM_d, saida0_q, saida1_q;
  wire [7:4] not_2_out;
  wire [9:0] cpu8bit1k_1_addrbus, cpu8bit1k_1_promaddr;

  DIV50M10HZ div50m10hz_1 (.Clock50M(Clock), .y(div50m10hz_1_y));
  ROM #(.AddrBits(10), .Bits(8)) PROM (.A(cpu8bit1k_1_promaddr), .sel(1'b1), .D(PROM_d));
  CPU8Bit1K cpu8bit1k_1 (
    .RST(Reset), .IN({8{1'b0}}), .Clock(div50m10hz_1_y), .PromIN(PROM_d), .OUT(cpu8bit1k_1_out),
    .AddrBus(cpu8bit1k_1_addrbus), .OutE(cpu8bit1k_1_oute), .PromAddr(cpu8bit1k_1_promaddr));  // open: InE
  not not_1 (not_1_out, cpu8bit1k_1_addrbus[0]);
  and and_1 (and_1_out, cpu8bit1k_1_addrbus[0], cpu8bit1k_1_oute);
  and and_2 (and_2_out, not_1_out, cpu8bit1k_1_oute);
  BasicReg8 saida1 (.Q(saida1_q), .D(cpu8bit1k_1_out), .E(and_1_out), .CLK(div50m10hz_1_y));
  BasicReg8 saida0 (.Q(saida0_q), .D(cpu8bit1k_1_out), .E(and_2_out), .CLK(div50m10hz_1_y));
  DIV50M100HZ div50m100hz_1 (.Clock50M(Clock), .y(dig0));
  assign {not_2_out, L3, L2, L1, L0} = ~saida1_q;  // Not not_2, 8 bits wide
  Multiplexer #(.Bits(4)) multiplexer_1 (
    .sel(dig0), .in_0(saida0_q[3:0]), .in_1(saida0_q[7:4]), .out(multiplexer_1_out));
  Driver7Seg driver7seg_1 (
    .D0(multiplexer_1_out[0]), .D1(multiplexer_1_out[1]), .D2(multiplexer_1_out[2]),
    .D3(multiplexer_1_out[3]), .Inv(1'b1), .a(a), .b(b), .c(c), .d(d), .e(e), .f(f), .g(g));
  not not_3 (dig1, dig0);

  // Notes on the sheet:
  //   Clock: Hz: 10
  //   contents of PROM (hex, n*v repeats v):
  //   3,0,21,a1,0,21,9,0,27
endmodule
